# Fritzing sketch Stackduino-fritzing-wiring-diagram-push-buttons (saved by Fritzing 0.8.0b)
breadboards: 1

parts:
  LCD1 = LCD screen
  Arduino1 = Arduino
  U1 = Optocoupler [package=THT]
  U2 = Optocoupler [package=THT]
  M1 = Stepper Motor - Bipolar
  Part1 = EasyDriver_v44
  R1 = 330 Ω Resistor [package=THT]
  R2 = 330 Ω Resistor [package=THT]
  R5 = Resistor [tolerance=±5% resistance=220 package=THT]
  R6 = Rotary Potentiometer (Small) [maximum_resistance=100kΩ]
  S3 = Pushbutton [package="[THT]"]
  S4 = Pushbutton [package="[THT]"]
  ENCODER1 = Rotary Encoder with Knob
  TRS1 = Audio Jack (TRS) 3.5mm [package="4Ucon 08780 [THT]"]
  S5 = Round Pushbutton
  S6 = Round Pushbutton
  S7 = Round Pushbutton

nets:
  GND: LCD1.VSS, LCD1.R/W, LCD1.LED-, Arduino1.GND, U1.Pin_2, U1.Pin_4, U2.Pin_2, U2.Pin_4, Part1.GND, R6.leg1, S3.Pin_1, S3.Pin_2, S4.Pin_3, S4.Pin_4, ENCODER1.no_name_yet#2, ENCODER1.no_name_yet#5, TRS1.Sleeve, S5.leg0, S7.leg1
  VDD: LCD1.VDD, Arduino1.+5V, R5.Pin_0, R6.leg2
  N1: LCD1.V0, R6.wiper
  N2: LCD1.RS, Arduino1.D8
  N3: LCD1.E, Arduino1.D9
  N4: LCD1.DB4, Arduino1.D10
  N5: LCD1.DB5, Arduino1.D11
  N6: LCD1.DB6, Arduino1.D12
  N7: LCD1.DB7, Arduino1.D13
  N8: Arduino1.D7, R2.Pin_1
  N9: Arduino1.D6, R1.Pin_1
  N10: Arduino1.D5, Part1.STEP
  N11: Arduino1.D4, Part1.DIR
  N12: Arduino1.D3, ENCODER1.no_name_yet#4
  N13: Arduino1.D2, S7.leg0
  N14: Arduino1.A0, ENCODER1.no_name_yet#3
  N15: Arduino1.A1, ENCODER1.no_name_yet#1
  N16: Arduino1.A2, S5.leg1
  N17: Arduino1.A4, S3.Pin_3, S4.Pin_1, S4.Pin_2
  N18: Arduino1.A5, S6.leg1
  N19: U1.Pin_1, R1.Pin_0
  N20: U1.Pin_5, TRS1.Ring
  N21: U2.Pin_1, R2.Pin_0
  N22: U2.Pin_5, TRS1.Tip
  N23: M1.A, Part1.OUT2A
  N24: M1.C, Part1.OUT2B
  N25: M1.B, Part1.OUT1A
  N26: M1.D, Part1.OUT1B

notes:
  3.5 stereo socket - shutter signal to camera
  Manual control - fwd
  Manual control - bwd
  Limit switches
  Optocouplers
  Easydriver
  16x2 LCD
  Rotary
  encoder
  Start/ stop stack

custom parts:
  330 Ω Resistor: A generic resistor (0.25W)
  Rotary Encoder with Knob: Rotary Encoder with 1/4" Shaft and Knob
